// Logisim project watch.circ as structural Verilog: 12 circuits, main circuit Electronic Block
module Electronic_Block (
  input  CLK,
  input  RW,
  input  RM,
  input  A,
  input  B,
  input  AB,
  output [2:0] S,
  output [1:0] I1,
  output [1:0] I2,
  output [6:0] H,
  output [6:0] h_2,
  output [6:0] M,
  output [6:0] m_2,
  output [6:0] S_2,
  output [6:0] s_3
);

  wire buttons_1_a_2, buttons_1_b_2, buttons_1_reg_en, MUX_Control, or_1_out, or_2_out, \Инк__минут ,
       \Инк__секунд , \Инк__часов , \Минуты_вкл_откл , \Подключ__CLK_к_секундомеру , \Подключ__CLK_к_часам ,
       \Сброс_секундомера , \Секунды_вкл_откл , \Часы_вкл_откл ;
  wire [2:0] fsm_with_reset_1_sn, register_1_q;
  wire [3:0] mux_1_hh, mux_1_hl, mux_1_mh, mux_1_ml, mux_1_sh, mux_1_sl;
  wire [6:0] indicator_transformer_1_out_2, indicator_transformer_2_out_2, indicator_transformer_3_out_2,
       indicator_transformer_4_out_2, indicator_transformer_5_out_2, indicator_transformer_6_out_2;
  wire [23:0] basic_watch_1_out_9, basic_watch_2_out_9;

  Pull_Resistor pull_resistor_1 (.node(RW));
  Pull_Resistor pull_resistor_2 (.node(RM));
  Buttons buttons_1 (.A(A), .B(B), .AB(AB), .a_2(buttons_1_a_2), .reg_en(buttons_1_reg_en), .b_2(buttons_1_b_2));
  Register #(.width(3), .trigger("low")) register_1 (
    .D(S), .Q(register_1_q), .clk(buttons_1_reg_en), .clr(RM));  // open: en
  Indicator_Control indicator_control_1 (
    .en(\Часы_вкл_откл ), .O(H), .o_2(h_2), .I(indicator_transformer_1_out_2),
    .i_2(indicator_transformer_2_out_2));
  Indicator_Transformer indicator_transformer_1 (.in_1(mux_1_hh), .out_2(indicator_transformer_1_out_2));
  Indicator_Transformer indicator_transformer_2 (.in_1(mux_1_hl), .out_2(indicator_transformer_2_out_2));
  Basic_Watch basic_watch_1 (
    .EN(\Подключ__CLK_к_часам ), .CLK(CLK), .h_plus_plus(\Инк__часов ), .m_plus_plus(\Инк__минут ),
    .s_plus_plus(\Инк__секунд ), ._0(RW), .out_9(basic_watch_1_out_9), .AB_crude(AB),
    ._0_EN(\Подключ__CLK_к_часам ));
  Indicator_Control indicator_control_2 (
    .en(\Минуты_вкл_откл ), .O(M), .o_2(m_2), .I(indicator_transformer_3_out_2),
    .i_2(indicator_transformer_5_out_2));
  Indicator_Transformer indicator_transformer_3 (.in_1(mux_1_mh), .out_2(indicator_transformer_3_out_2));
  FSM_with_reset fsm_with_reset_1 (
    .a(buttons_1_a_2), .b(buttons_1_b_2), .Sc(register_1_q), .Sn(fsm_with_reset_1_sn), .yh(\Инк__часов ),
    .ym(\Инк__минут ), .ys(\Инк__секунд ), .yr(\Сброс_секундомера ));
  Register #(.width(3), .trigger("high")) register_2 (
    .D(fsm_with_reset_1_sn), .Q(S), .clk(buttons_1_reg_en), .clr(RM));  // open: en
  Indicator_Transformer indicator_transformer_4 (.in_1(mux_1_sh), .out_2(indicator_transformer_4_out_2));
  Indicator_Transformer indicator_transformer_5 (.in_1(mux_1_ml), .out_2(indicator_transformer_5_out_2));
  MUX mux_1 (
    .C(MUX_Control), .C_0(basic_watch_1_out_9), .C_1(basic_watch_2_out_9), .HH(mux_1_hh), .HL(mux_1_hl),
    .MH(mux_1_mh), .ML(mux_1_ml), .SH(mux_1_sh), .SL(mux_1_sl));
  Basic_Watch basic_watch_2 (
    .EN(\Подключ__CLK_к_секундомеру ), .CLK(CLK), ._0(\Сброс_секундомера ), .out_9(basic_watch_2_out_9),
    .AB_crude(AB), ._0_EN(or_1_out));  // open: h_plus_plus, m_plus_plus, s_plus_plus
  or or_1 (or_1_out, \Сброс_секундомера , \Подключ__CLK_к_секундомеру );
  Potential_Decoder potential_decoder_1 (
    .dh(\Часы_вкл_откл ), .dm(\Минуты_вкл_откл ), .ds(\Секунды_вкл_откл ), .cw(\Подключ__CLK_к_часам ),
    .csw(\Подключ__CLK_к_секундомеру ), .mux(MUX_Control), .S(S));
  Indicator_Control indicator_control_3 (
    .en(\Секунды_вкл_откл ), .O(S_2), .o_2(s_3), .I(indicator_transformer_4_out_2),
    .i_2(indicator_transformer_6_out_2));
  Indicator_Transformer indicator_transformer_6 (.in_1(mux_1_sl), .out_2(indicator_transformer_6_out_2));
  or or_2 (or_2_out, \Часы_вкл_откл , \Минуты_вкл_откл , \Секунды_вкл_откл );
  Delimiter delimiter_1 (.clk(CLK), .out_3(I1), .en(or_2_out));

  assign I2 = I1;

  // Other names for the same wires on the sheet: Сброс_памяти = RM; Сброс_сч_ов_часов = RW; Тактовый_генератор = CLK
endmodule

module Indicator_Transformer (
  input  [3:0] in_1,
  output [6:0] out_2
);

  wire and_1_out, and_2_out, and_3_out, and_4_out, and_5_out, and_6_out, and_7_out, and_8_out, and_9_out,
       and_10_out, and_11_out, and_12_out, and_13_out, and_14_out, and_15_out, and_16_out, not_1_out,
       not_2_out, not_3_out, not_4_out, not_5_out, not_6_out, not_7_out, not_8_out, not_9_out, not_10_out,
       not_11_out, not_12_out, not_13_out, not_14_out, not_15_out, not_16_out, not_17_out, not_18_out,
       not_19_out, not_20_out, not_21_out;

  not not_1 (not_1_out, in_1[2]);
  and and_1 (and_1_out, not_1_out, in_1[1]);
  and and_2 (and_2_out, in_1[2], not_2_out);
  not not_2 (not_2_out, in_1[1]);
  and and_3 (and_3_out, in_1[2], not_3_out);
  not not_3 (not_3_out, in_1[0]);
  not not_4 (not_4_out, in_1[1]);
  and and_4 (and_4_out, not_4_out, not_5_out);
  not not_5 (not_5_out, in_1[0]);
  and and_5 (and_5_out, in_1[2], not_6_out);
  not not_6 (not_6_out, in_1[1]);
  and and_6 (and_6_out, in_1[2], not_7_out);
  not not_7 (not_7_out, in_1[0]);
  not not_8 (not_8_out, in_1[2]);
  and and_7 (and_7_out, not_8_out, not_9_out);
  not not_9 (not_9_out, in_1[0]);
  and and_8 (and_8_out, in_1[2], in_1[0]);
  not not_10 (not_10_out, in_1[2]);
  not not_11 (not_11_out, in_1[1]);
  and and_9 (and_9_out, not_11_out, not_12_out);
  not not_12 (not_12_out, in_1[0]);
  and and_10 (and_10_out, in_1[1], in_1[0]);
  not not_13 (not_13_out, in_1[1]);
  or or_1 (out_2[4], not_13_out, in_1[0], in_1[2]);
  not not_14 (not_14_out, in_1[2]);
  and and_11 (and_11_out, not_14_out, not_15_out);
  not not_15 (not_15_out, in_1[0]);
  not not_16 (not_16_out, in_1[2]);
  and and_12 (and_12_out, not_16_out, in_1[1]);
  and and_13 (and_13_out, in_1[1], not_17_out);
  not not_17 (not_17_out, in_1[0]);
  not not_18 (not_18_out, in_1[1]);
  and and_14 (and_14_out, in_1[2], not_18_out, in_1[0]);
  not not_19 (not_19_out, in_1[2]);
  and and_15 (and_15_out, not_19_out, not_20_out);
  not not_20 (not_20_out, in_1[0]);
  and and_16 (and_16_out, in_1[1], not_21_out);
  not not_21 (not_21_out, in_1[0]);
  or or_2 (out_2[0], and_1_out, and_2_out, and_3_out, in_1[3]);
  or or_3 (out_2[1], and_4_out, and_5_out, and_6_out, in_1[3]);
  or or_4 (out_2[2], and_7_out, in_1[1], and_8_out, in_1[3]);
  or or_5 (out_2[3], not_10_out, and_9_out, and_10_out);
  or or_6 (out_2[5], and_11_out, and_12_out, and_13_out, and_14_out, in_1[3]);
  or or_7 (out_2[6], and_15_out, and_16_out);
endmodule

module MUX (
  input  C,
  input  [23:0] C_0,
  input  [23:0] C_1,
  output [3:0] HH,
  output [3:0] HL,
  output [3:0] MH,
  output [3:0] ML,
  output [3:0] SH,
  output [3:0] SL
);

  wire not_1_out;

  assign {HH, HL, MH, ML, SH, SL} = not_1_out ? C_0 : 24'bz;  // Controlled_Buffer controlled_buffer_1
  not not_1 (not_1_out, C);
  assign {HH, HL, MH, ML, SH, SL} = C ? C_1 : 24'bz;  // Controlled_Buffer controlled_buffer_2
endmodule

module Delimiter (
  input  en,
  input  clk,
  output [1:0] out_3
);

  wire not_1_out, pull_resistor_1_node;

  assign out_3 = not_1_out ? 2'b00 : 2'bz;  // Controlled_Buffer controlled_buffer_1
  not not_1 (not_1_out, pull_resistor_1_node);
  Pull_Resistor pull_resistor_1 (.node(pull_resistor_1_node));
  assign pull_resistor_1_node = en ? clk : 1'bz;  // Controlled_Buffer controlled_buffer_2
  assign out_3 = pull_resistor_1_node ? 2'b11 : 2'bz;  // Controlled_Buffer controlled_buffer_3
endmodule

module Comparator_w__4 (
  input  [3:0] in_1,
  output out_2
);

  wire [3:0] xnor_1_out;

  assign xnor_1_out = ~(in_1 ^ 4'b0100);  // XNOR_Gate xnor_1, 4 bits wide
  and and_1 (out_2, xnor_1_out[0], xnor_1_out[1], xnor_1_out[2], xnor_1_out[3]);
endmodule

module Potential_Decoder (
  input  [2:0] S,
  output dh,
  output dm,
  output ds,
  output cw,
  output csw,
  output mux
);

  wire and_3_out, and_4_out, and_5_out, and_6_out, and_7_out, and_8_out, and_9_out, and_10_out, and_11_out,
       and_12_out, and_13_out, not_1_out, not_2_out, not_3_out, not_4_out, not_5_out, not_6_out, not_7_out,
       not_8_out, not_9_out, not_10_out, not_11_out, not_12_out;

  not not_1 (not_1_out, S[2]);
  not not_2 (not_2_out, S[1]);
  not not_3 (not_3_out, S[2]);
  not not_4 (not_4_out, S[2]);
  not not_5 (not_5_out, S[1]);
  not not_6 (not_6_out, S[1]);
  not not_7 (not_7_out, S[0]);
  not not_8 (not_8_out, S[2]);
  not not_9 (not_9_out, S[1]);
  not not_10 (not_10_out, S[1]);
  not not_11 (not_11_out, S[2]);
  not not_12 (not_12_out, S[0]);
  and and_1 (csw, S[2], S[1], S[0]);
  and and_2 (mux, S[2], S[1]);
  and and_3 (and_3_out, not_1_out, not_2_out);
  and and_4 (and_4_out, not_3_out, S[0]);
  and and_5 (and_5_out, S[2], S[1]);
  and and_6 (and_6_out, not_4_out, not_5_out);
  and and_7 (and_7_out, not_6_out, not_7_out);
  and and_8 (and_8_out, S[2], S[1]);
  and and_9 (and_9_out, not_8_out, not_9_out);
  and and_10 (and_10_out, not_10_out, S[0]);
  and and_11 (and_11_out, S[2], S[1]);
  and and_12 (and_12_out, not_11_out, not_12_out);
  and and_13 (and_13_out, S[2], S[1]);
  or or_1 (dh, and_3_out, and_4_out, and_5_out);
  or or_2 (dm, and_6_out, and_7_out, and_8_out);
  or or_3 (ds, and_9_out, and_10_out, and_11_out);
  or or_4 (cw, and_12_out, and_13_out);
endmodule

module FSM (
  input  a,
  input  b,
  input  [2:0] Sc,
  output [2:0] Sn,
  output yh,
  output ym,
  output ys,
  output yr
);

  wire and_1_out, and_2_out, and_3_out, and_4_out, and_5_out, and_6_out, and_7_out, and_8_out, and_9_out,
       and_10_out, and_11_out, and_12_out, and_13_out, and_14_out, and_15_out, and_16_out, and_17_out,
       and_18_out, not_1_out, not_2_out, not_3_out, not_4_out, not_5_out, not_6_out, not_7_out, not_8_out,
       not_9_out, not_10_out, not_11_out, not_12_out, not_13_out, not_14_out, not_15_out, not_16_out,
       not_17_out, not_18_out, not_19_out, not_20_out, not_21_out, not_22_out, not_23_out, not_24_out,
       not_25_out, not_26_out, not_27_out, not_28_out, not_29_out, not_30_out, not_31_out, not_32_out,
       not_33_out, not_34_out;

  not not_1 (not_1_out, a);
  not not_2 (not_2_out, b);
  not not_3 (not_3_out, Sc[0]);
  not not_4 (not_4_out, b);
  not not_5 (not_5_out, Sc[1]);
  not not_6 (not_6_out, Sc[0]);
  not not_7 (not_7_out, a);
  not not_8 (not_8_out, b);
  not not_9 (not_9_out, b);
  not not_10 (not_10_out, Sc[0]);
  not not_11 (not_11_out, a);
  not not_12 (not_12_out, b);
  not not_13 (not_13_out, Sc[2]);
  not not_14 (not_14_out, Sc[1]);
  not not_15 (not_15_out, Sc[0]);
  not not_16 (not_16_out, b);
  not not_17 (not_17_out, Sc[2]);
  not not_18 (not_18_out, Sc[0]);
  not not_19 (not_19_out, a);
  not not_20 (not_20_out, b);
  not not_21 (not_21_out, a);
  not not_22 (not_22_out, b);
  not not_23 (not_23_out, Sc[1]);
  not not_24 (not_24_out, b);
  not not_25 (not_25_out, Sc[0]);
  not not_26 (not_26_out, Sc[2]);
  not not_27 (not_27_out, a);
  not not_28 (not_28_out, Sc[2]);
  not not_29 (not_29_out, a);
  not not_30 (not_30_out, Sc[1]);
  not not_31 (not_31_out, Sc[0]);
  not not_32 (not_32_out, a);
  not not_33 (not_33_out, Sc[1]);
  not not_34 (not_34_out, a);
  and and_1 (and_1_out, not_1_out, Sc[2]);
  and and_2 (and_2_out, not_2_out, Sc[2], not_3_out);
  and and_3 (and_3_out, b, Sc[2], Sc[0]);
  and and_4 (and_4_out, a, not_4_out, Sc[1], Sc[0]);
  and and_5 (and_5_out, a, b, not_5_out, not_6_out);
  and and_6 (and_6_out, not_7_out, not_8_out, Sc[1]);
  and and_7 (and_7_out, not_9_out, Sc[1], not_10_out);
  and and_8 (and_8_out, not_11_out, Sc[2], Sc[1]);
  and and_9 (and_9_out, not_12_out, Sc[2], Sc[1]);
  and and_10 (and_10_out, b, not_13_out, not_14_out, not_15_out);
  and and_11 (and_11_out, b, Sc[1], Sc[0]);
  and and_12 (and_12_out, a, not_16_out, not_17_out, not_18_out);
  and and_13 (and_13_out, not_19_out, not_20_out, Sc[0]);
  and and_14 (and_14_out, not_21_out, Sc[1], Sc[0]);
  and and_15 (and_15_out, b, Sc[2], Sc[0]);
  and and_16 (and_16_out, a, not_22_out, not_23_out);
  and and_17 (and_17_out, a, not_24_out, Sc[2], not_25_out);
  and and_18 (and_18_out, a, b, not_26_out, Sc[1]);
  and and_19 (yh, not_27_out, b, not_28_out, Sc[1], Sc[0]);
  and and_20 (ym, not_29_out, b, Sc[2], not_30_out, not_31_out);
  and and_21 (ys, not_32_out, b, Sc[2], not_33_out, Sc[0]);
  and and_22 (yr, not_34_out, b, Sc[2], Sc[1]);
  or or_1 (Sn[2], and_1_out, and_2_out, and_3_out, and_4_out, and_5_out);
  or or_2 (Sn[1], and_6_out, and_7_out, and_8_out, and_9_out, and_10_out, and_11_out, and_12_out);
  or or_3 (Sn[0], and_13_out, and_14_out, and_15_out, and_16_out, and_17_out, and_18_out);
endmodule

module Basic_Watch (
  input  EN,
  input  CLK,
  input  h_plus_plus,
  input  m_plus_plus,
  input  s_plus_plus,
  input  _0_EN,
  input  _0,
  input  AB_crude,
  output [23:0] out_9
);

  wire and_1_out, and_2_out, and_3_out, and_4_out, comparator_w_4_1_out_2, counter_1_carry, counter_2_carry,
       counter_3_carry, counter_4_carry, counter_5_carry, counter_6_carry, not_1_out, or_1_out, or_2_out,
       or_3_out, or_4_out, pull_resistor_3_node, pull_resistor_5_node;

  Counter #(.width(4), .max('h2), .trigger("falling")) counter_1 (
    .Q(out_9[23:20]), .carry(counter_1_carry), .clk(counter_2_carry), .clr(or_2_out));  // open: load, D, count
  Comparator_w__4 comparator_w_4_1 (.in_1(out_9[19:16]), .out_2(comparator_w_4_1_out_2));
  and and_1 (and_1_out, comparator_w_4_1_out_2, counter_1_carry);
  Counter #(.width(4), .max('h9), .trigger("falling")) counter_2 (
    .Q(out_9[19:16]), .carry(counter_2_carry), .clk(and_2_out), .clr(or_2_out));  // open: load, D, count
  or or_1 (or_1_out, counter_3_carry, h_plus_plus);
  or or_2 (or_2_out, and_1_out, _0);
  and and_2 (and_2_out, not_1_out, or_1_out);
  not not_1 (not_1_out, AB_crude);
  Counter #(.width(4), .max('h5), .trigger("falling")) counter_3 (
    .Q(out_9[15:12]), .carry(counter_3_carry), .clk(counter_4_carry), .clr(pull_resistor_5_node));  // open: load, D, count
  Pull_Resistor pull_resistor_1 (.node(h_plus_plus));
  Counter #(.width(4), .max('h9), .trigger("falling")) counter_4 (
    .Q(out_9[11:8]), .carry(counter_4_carry), .clk(and_3_out), .clr(pull_resistor_5_node));  // open: load, D, count
  or or_3 (or_3_out, counter_5_carry, m_plus_plus);
  and and_3 (and_3_out, not_1_out, or_3_out);
  Counter #(.width(4), .max('h5), .trigger("falling")) counter_5 (
    .Q(out_9[7:4]), .carry(counter_5_carry), .clk(counter_6_carry), .clr(pull_resistor_5_node));  // open: load, D, count
  Pull_Resistor pull_resistor_2 (.node(m_plus_plus));
  Counter #(.width(4), .max('h9), .trigger("falling")) counter_6 (
    .Q(out_9[3:0]), .carry(counter_6_carry), .clk(and_4_out), .clr(pull_resistor_5_node));  // open: load, D, count
  Pull_Resistor pull_resistor_3 (.node(pull_resistor_3_node));
  or or_4 (or_4_out, pull_resistor_3_node, s_plus_plus);
  Pull_Resistor pull_resistor_4 (.node(s_plus_plus));
  Pull_Resistor pull_resistor_5 (.node(pull_resistor_5_node));
  assign pull_resistor_5_node = _0_EN ? or_2_out : 1'bz;  // Controlled_Buffer controlled_buffer_1
  and and_4 (and_4_out, not_1_out, or_4_out);
  assign pull_resistor_3_node = EN ? CLK : 1'bz;  // Controlled_Buffer controlled_buffer_2
endmodule

module Indicator_Control (
  input  en,
  input  [6:0] I,
  input  [6:0] i_2,
  output [6:0] O,
  output [6:0] o_2
);

  Pull_Resistor pull_resistor_1 (.node({O, o_2}));
  assign {O, o_2} = en ? {I, i_2} : 14'bz;  // Controlled_Buffer controlled_buffer_1
endmodule

module Buttons (
  input  A,
  input  B,
  input  AB,
  output a_2,
  output reg_en,
  output b_2
);

  or or_1 (a_2, A, AB);
  or or_2 (reg_en, a_2, b_2);
  or or_3 (b_2, B, AB);
endmodule

module FSM_with_reset (
  input  a,
  input  b,
  input  [2:0] Sc,
  output [2:0] Sn,
  output yh,
  output ym,
  output ys,
  output yr
);

  wire and_1_out, and_2_out, and_3_out, and_4_out, and_5_out, and_6_out, and_7_out, and_8_out, and_9_out,
       and_10_out, and_11_out, and_12_out, and_13_out, and_14_out, and_15_out, and_16_out, and_17_out,
       and_18_out, and_22_out, and_23_out, not_1_out, not_2_out, not_3_out, not_4_out, not_5_out, not_6_out,
       not_7_out, not_8_out, not_9_out, not_10_out, not_11_out, not_12_out, not_13_out, not_14_out,
       not_15_out, not_16_out, not_17_out, not_18_out, not_19_out, not_20_out, not_21_out, not_22_out,
       not_23_out, not_24_out, not_25_out, not_26_out, not_27_out, not_28_out, not_29_out, not_30_out,
       not_31_out, not_32_out, not_33_out, not_34_out, not_35_out, not_36_out, not_37_out;

  not not_1 (not_1_out, a);
  not not_2 (not_2_out, b);
  not not_3 (not_3_out, Sc[0]);
  not not_4 (not_4_out, Sc[1]);
  not not_5 (not_5_out, b);
  not not_6 (not_6_out, Sc[1]);
  not not_7 (not_7_out, Sc[0]);
  not not_8 (not_8_out, a);
  not not_9 (not_9_out, b);
  not not_10 (not_10_out, b);
  not not_11 (not_11_out, Sc[0]);
  not not_12 (not_12_out, a);
  not not_13 (not_13_out, b);
  not not_14 (not_14_out, Sc[2]);
  not not_15 (not_15_out, Sc[1]);
  not not_16 (not_16_out, Sc[0]);
  not not_17 (not_17_out, Sc[2]);
  not not_18 (not_18_out, b);
  not not_19 (not_19_out, Sc[2]);
  not not_20 (not_20_out, Sc[0]);
  not not_21 (not_21_out, b);
  not not_22 (not_22_out, Sc[1]);
  not not_23 (not_23_out, a);
  not not_24 (not_24_out, Sc[1]);
  not not_25 (not_25_out, b);
  not not_26 (not_26_out, Sc[1]);
  not not_27 (not_27_out, b);
  not not_28 (not_28_out, Sc[0]);
  not not_29 (not_29_out, Sc[2]);
  not not_30 (not_30_out, a);
  not not_31 (not_31_out, Sc[2]);
  not not_32 (not_32_out, a);
  not not_33 (not_33_out, Sc[1]);
  not not_34 (not_34_out, Sc[0]);
  not not_35 (not_35_out, a);
  not not_36 (not_36_out, Sc[1]);
  not not_37 (not_37_out, a);
  and and_1 (and_1_out, not_1_out, Sc[2]);
  and and_2 (and_2_out, not_2_out, Sc[2], not_3_out);
  and and_3 (and_3_out, b, Sc[2], not_4_out);
  and and_4 (and_4_out, a, not_5_out, Sc[1], Sc[0]);
  and and_5 (and_5_out, a, b, not_6_out, not_7_out);
  and and_6 (and_6_out, not_8_out, not_9_out, Sc[1]);
  and and_7 (and_7_out, not_10_out, Sc[1], not_11_out);
  and and_8 (and_8_out, not_12_out, Sc[2], Sc[1]);
  and and_9 (and_9_out, not_13_out, Sc[2], Sc[1]);
  and and_10 (and_10_out, b, not_14_out, not_15_out, not_16_out);
  and and_11 (and_11_out, b, not_17_out, Sc[1], Sc[0]);
  and and_12 (and_12_out, a, not_18_out, not_19_out, not_20_out);
  and and_13 (and_13_out, not_21_out, not_22_out, Sc[0]);
  and and_14 (and_14_out, not_23_out, Sc[1], Sc[0]);
  and and_15 (and_15_out, Sc[2], not_24_out, Sc[0]);
  and and_16 (and_16_out, a, not_25_out, not_26_out);
  and and_17 (and_17_out, a, not_27_out, Sc[2], not_28_out);
  and and_18 (and_18_out, a, b, not_29_out, Sc[1]);
  and and_19 (yh, not_30_out, b, not_31_out, Sc[1], Sc[0]);
  and and_20 (ym, not_32_out, b, Sc[2], not_33_out, not_34_out);
  and and_21 (ys, not_35_out, b, Sc[2], not_36_out, Sc[0]);
  and and_22 (and_22_out, not_37_out, b, Sc[2], Sc[1]);
  and and_23 (and_23_out, b, Sc[2], Sc[1], Sc[0]);
  or or_1 (Sn[2], and_1_out, and_2_out, and_3_out, and_4_out, and_5_out);
  or or_2 (Sn[1], and_6_out, and_7_out, and_8_out, and_9_out, and_10_out, and_11_out, and_12_out);
  or or_3 (Sn[0], and_13_out, and_14_out, and_15_out, and_16_out, and_17_out, and_18_out);
  or or_4 (yr, and_22_out, and_23_out);
endmodule

module main (
);

  wire A_out, AB_out, B_out, clock_1_out, RM_out, RW_out;
  wire [1:0] electronic_block_1_i1, electronic_block_1_i2;
  wire [2:0] electronic_block_1_h_2, electronic_block_1_h_2_3, electronic_block_1_m_2,
       electronic_block_1_m_2_3, electronic_block_1_s, electronic_block_1_s_2_2, electronic_block_1_s_3_2;
  wire [3:0] bit_extender_1_out, electronic_block_1_h, electronic_block_1_h_2_2, electronic_block_1_m,
       electronic_block_1_m_2_2, electronic_block_1_s_2, electronic_block_1_s_3;

  Electronic_Block electronic_block_1 (
    .CLK(clock_1_out), .RW(RW_out), .RM(RM_out), .A(A_out), .B(B_out), .AB(AB_out),
    .H({electronic_block_1_h_2, electronic_block_1_h}),
    .h_2({electronic_block_1_h_2_3, electronic_block_1_h_2_2}),
    .M({electronic_block_1_m_2, electronic_block_1_m}),
    .m_2({electronic_block_1_m_2_3, electronic_block_1_m_2_2}),
    .S_2({electronic_block_1_s_2_2, electronic_block_1_s_2}),
    .s_3({electronic_block_1_s_3_2, electronic_block_1_s_3}), .I1(electronic_block_1_i1),
    .I2(electronic_block_1_i2), .S(electronic_block_1_s));
  Button A (.out(A_out));
  Button B (.out(B_out));
  Button AB (.out(AB_out));
  _7_Segment_Display u_7_segment_display_1 (
    .g(electronic_block_1_h[0]), .f(electronic_block_1_h[1]), .a(electronic_block_1_h[2]),
    .b(electronic_block_1_h[3]), .e(electronic_block_1_h_2[2]), .d(electronic_block_1_h_2[1]),
    .c(electronic_block_1_h_2[0]));  // open: dp
  _7_Segment_Display u_7_segment_display_2 (
    .g(electronic_block_1_h_2_2[0]), .f(electronic_block_1_h_2_2[1]), .a(electronic_block_1_h_2_2[2]),
    .b(electronic_block_1_h_2_2[3]), .e(electronic_block_1_h_2_3[2]), .d(electronic_block_1_h_2_3[1]),
    .c(electronic_block_1_h_2_3[0]));  // open: dp
  _7_Segment_Display u_7_segment_display_3 (
    .g(electronic_block_1_m[0]), .f(electronic_block_1_m[1]), .a(electronic_block_1_m[2]),
    .b(electronic_block_1_m[3]), .e(electronic_block_1_m_2[2]), .d(electronic_block_1_m_2[1]),
    .c(electronic_block_1_m_2[0]));  // open: dp
  DotMatrix #(.matrixcols(1), .matrixrows(2), .dotshape("circle")) dotmatrix_1 (.col0(electronic_block_1_i2));
  _7_Segment_Display u_7_segment_display_4 (
    .g(electronic_block_1_m_2_2[0]), .f(electronic_block_1_m_2_2[1]), .a(electronic_block_1_m_2_2[2]),
    .b(electronic_block_1_m_2_2[3]), .e(electronic_block_1_m_2_3[2]), .d(electronic_block_1_m_2_3[1]),
    .c(electronic_block_1_m_2_3[0]));  // open: dp
  DotMatrix #(.matrixcols(1), .matrixrows(2), .dotshape("circle")) dotmatrix_2 (.col0(electronic_block_1_i1));
  _7_Segment_Display u_7_segment_display_5 (
    .g(electronic_block_1_s_3[0]), .f(electronic_block_1_s_3[1]), .a(electronic_block_1_s_3[2]),
    .b(electronic_block_1_s_3[3]), .e(electronic_block_1_s_3_2[2]), .d(electronic_block_1_s_3_2[1]),
    .c(electronic_block_1_s_3_2[0]));  // open: dp
  _7_Segment_Display u_7_segment_display_6 (
    .g(electronic_block_1_s_2[0]), .f(electronic_block_1_s_2[1]), .a(electronic_block_1_s_2[2]),
    .b(electronic_block_1_s_2[3]), .e(electronic_block_1_s_2_2[2]), .d(electronic_block_1_s_2_2[1]),
    .c(electronic_block_1_s_2_2[0]));  // open: dp
  Clock clock_1 (.out(clock_1_out));
  Button RW (.out(RW_out));
  Button RM (.out(RM_out));
  Hex_Digit_Display hex_digit_display_1 (.value(bit_extender_1_out));  // open: dp
  assign bit_extender_1_out = {{1{1'b0}}, electronic_block_1_s};  // Bit_Extender bit_extender_1
endmodule
